# Fritzing sketch archi_forgette_schema_JOLI (saved by Fritzing 0.9.5d)
breadboards: 1

parts:
  Raspberry_Pi_1 = Raspberry Pi 3 [part_number=RPI-3-V1.2]
  pH_Circuit1 = pH Circuit
  LED1 = RGB LED (com. anode, rbg) [package="5 mm [THT]"]
  LED2 = RGB LED (com. anode, rbg) [package="5 mm [THT]"]
  DS2 = DS18B20 1-Wire Temperature Sensor [part_number=DS18B20]
  R1 = Resistor [tolerance=±5% resistance=220 package="2010 [SMD]"]
  R2 = Resistor [tolerance=±5% resistance=220 package="2010 [SMD]"]
  R3 = Resistor [tolerance=±5% resistance=220 package="2010 [SMD]"]
  R4 = Resistor [tolerance=±5% resistance=220 package="2010 [SMD]"]
  R5 = Resistor [tolerance=±5% resistance=220 package="2010 [SMD]"]
  R6 = Resistor [tolerance=±5% resistance=220 package="2010 [SMD]"]

nets:
  N1: Raspberry_Pi_1.GPIO2, pH_Circuit1.TX
  N2: Raspberry_Pi_1.GPIO3, pH_Circuit1.RX
  N3: Raspberry_Pi_1.GIPO4, R1.Pin_1
  N4: Raspberry_Pi_1.GIPO17, R2.Pin_1
  N5: Raspberry_Pi_1.GIPO27, R3.Pin_1
  N6: Raspberry_Pi_1.GIPO13, R4.Pin_1
  N7: Raspberry_Pi_1.GIPO19, R5.Pin_1
  N8: Raspberry_Pi_1.GIPO26, R6.Pin_1
  GND: Raspberry_Pi_1.GND, pH_Circuit1.GND, DS2.GND
  N9: Raspberry_Pi_1.GIPO24, DS2.DQ
  5V: Raspberry_Pi_1.5V, pH_Circuit1.Vcc, LED1.common_anode, LED2.common_anode, DS2.VDD
  N10: LED1.red_cathode, R3.Pin_0
  N11: LED1.blue_cathode, R2.Pin_0
  N12: LED1.green_cathode, R1.Pin_0
  N13: LED2.red_cathode, R6.Pin_0
  N14: LED2.blue_cathode, R5.Pin_0
  N15: LED2.green_cathode, R4.Pin_0
